# Fritzing sketch alarm_system_blueprint (saved by Fritzing 0.9.10b)
breadboards: 1

parts:
  Nano1 = Arduino Nano v2.3
  LED1 = LED - 5mm [color="Red (633nm)" current=0.030 package="5 mm [THT]"]
  R1 = Resistor [tolerance=±5% resistance=1k package="0603 [SMD]"]
  R2 = Resistor [tolerance=±5% resistance=1k package="0603 [SMD]"]
  LED2 = LED - 5mm [color="Green (555nm)" current=0.030 package="5 mm [THT]"]
  OLED_I2C1 = OLED 128x64 I2C Monochrome Display
  IR1 = TSOP312.., 314.. [package=THT]
  J3 = Basic Servo
  R3 = PHOTOCELL [package=photocell-kit]
  R4 = Resistor [tolerance=±5% resistance=1k package="0603 [SMD]"]
  J4 = Piezo Speaker
  Part1 = RFID-RC522-v2

nets:
  N1: Nano1.D2, IR1.Data
  N2: Nano1.D6, LED2.anode
  N3: Nano1.D7, LED1.anode
  N4: Nano1.D9, Part1.RST
  N5: Nano1.D10, Part1.SDA
  N6: Nano1.D11, Part1.MOSI
  N7: Nano1.D12, Part1.MISO
  N8: Nano1.D13, Part1.SCK
  N9: Nano1.A5, OLED_I2C1.SCK
  N10: Nano1.A4, OLED_I2C1.SDA
  N11: Nano1.A0, R3.P$2, R4.Pin_1
  +5V: Nano1.+5V, OLED_I2C1.VDD, IR1.Vs, J3.vcc, R3.P$1
  GND: Nano1.GND, R1.Pin_0, R2.Pin_0, OLED_I2C1.GND, IR1.GND, J3.gnd, R4.Pin_0, J4.pin1
  N12: LED1.cathode, R2.Pin_1
  N13: R1.Pin_1, LED2.cathode

custom parts:
  RFID-RC522-v2: A simple China made RFID-RC522 Reader; do check the pin labels, as this is a MFRC522 based clone.
